// Logisim project IA49MIPS.circ as structural Verilog: 9 circuits, main circuit TG00MIPS
module TG00MIPS (
);

  wire CLK_out, mips_1_halt, stopclk_1_clkout;

  Clock #(.highDuration(2), .lowDuration(2)) CLK (.out(CLK_out));
  StopClk stopclk_1 (.halt(mips_1_halt), .clkin(CLK_out), .clkout(stopclk_1_clkout));
  MIPS mips_1 (.clk(stopclk_1_clkout), .reset(1'b0), .halt(mips_1_halt));
endmodule

// clk
module MIPS (
  input  clk,
  input  reset,
  output halt
);

  wire ADDI, alu_1_z, ALUr, BEQ, EX_MEM_7_q, EX_MEM_13_q, EX_MEM_q, HALT_t, ID_EX_3_q, ID_EX_5_q, ID_EX_6_q,
       ID_EX_9_q, ID_EX_10_q, ID_EX_17_q, ID_EX_18_q, ID_EX_q, J, K1, K2, K3, K4, not_1_out, or_1_out,
       or_2_out, RM, RMm, unidad_de_control_1_wm, unidad_de_control_1_wr, WD, WM, WR, Z;
  wire [0:0] and_1_out;
  wire [2:0] OpALU;
  wire [3:0] control_alu_1_out, ID_EX_13_q_2;
  wire [4:0] EX_MEM_5_q, ID_EX_7_q, ID_EX_8_q, multiplexer_2_out, rd, rs, rt, WriteReg;
  wire [5:0] funcion, ID_EX_16_q, OPCODE;
  wire [15:0] desp;
  wire [25:0] ID_EX_14_q, Jin;
  wire [27:0] ID_EX_13_q;
  wire [31:0] A, adder_2_out, alu_1_result, ALUresul, B, BEQsalto, bit_extender_1_out,
       data_memory_32_1_read_data, EX_MEM_12_q, ExSig_desp, ExSig_dir___2, IF_ID_2_q, IF_ID_q,
       instruction_memory_1_instruction, Jump, MEM_WB_2_q, multiplexer_3_out, PC_4, PC_plus, PC_q, R_rt,
       Rdata, register_file_1_read_data_1, register_file_1_read_data_2;

  UNIDAD_DE_CONTROL unidad_de_control_1 (
    .OPCODE(OPCODE), .HALT(HALT_t), .J(J), .WR(unidad_de_control_1_wr), .RM(RMm),
    .WM(unidad_de_control_1_wm), .ALU(ALUr), .ADDI(ADDI), .BEQ(BEQ));
  Adder #(.width(32)) adder_1 (.a(32'h4), .b(PC_q), .out(PC_4));  // open: cin, cout
  Register #(.width(32)) PC (.D(PC_plus), .Q(PC_q), .clk(clk));  // open: en, clr
  Instruction_memory instruction_memory_1 (.Read_address(PC_q), .Instruction(instruction_memory_1_instruction));
  Multiplexer #(.select(2), .width(32), .enable("false")) multiplexer_1 (
    .in0(PC_4), .in1(BEQsalto), .in2(Jump), .out(PC_plus), .sel({K4, and_1_out[0]}));  // open: in3
  and and_1 (and_1_out[0], K3, Z);
  Register #(.width(1)) ID_EX (.D(unidad_de_control_1_wr), .Q(ID_EX_q), .clk(clk));  // open: en, clr
  Register #(.width(1)) EX_MEM (.D(ID_EX_q), .Q(EX_MEM_q), .clk(clk));  // open: en, clr
  Register #(.width(1)) ID_EX_2 (.D(ALUr), .Q(K1), .clk(clk));  // open: en, clr
  // Probe on instruction_memory_1_instruction
  Register #(.width(32)) IF_ID (.D(instruction_memory_1_instruction), .Q(IF_ID_q), .clk(clk));  // open: en, clr
  Register #(.width(1)) MEM_WB (.D(EX_MEM_q), .Q(WR), .clk(clk));  // open: en, clr
  Register #(.width(1)) ID_EX_3 (.D(unidad_de_control_1_wm), .Q(ID_EX_3_q), .clk(clk));  // open: en, clr
  InstDecoder instdecoder_1 (
    .IB(IF_ID_q), .IB31_26(OPCODE), .IB25_21(rs), .IB20_16(rt), .IB15_11(rd), .IB5_0(funcion), .IB15_0(desp),
    .IB25_0(Jin));
  Register #(.width(1)) EX_MEM_2 (.D(ID_EX_3_q), .Q(WM), .clk(clk));  // open: en, clr
  Register #(.width(1)) ID_EX_4 (.D(BEQ), .Q(K2), .clk(clk));  // open: en, clr
  Register #(.width(1)) ID_EX_5 (.D(BEQ), .Q(ID_EX_5_q), .clk(clk));  // open: en, clr
  Register #(.width(1)) ID_EX_6 (.D(RMm), .Q(ID_EX_6_q), .clk(clk));  // open: en, clr
  Register #(.width(1)) EX_MEM_3 (.D(ID_EX_6_q), .Q(RM), .clk(clk));  // open: en, clr
  Register #(.width(1)) EX_MEM_4 (.D(ID_EX_5_q), .Q(K3), .clk(clk));  // open: en, clr
  Register #(.width(5)) ID_EX_7 (.D(rt), .Q(ID_EX_7_q), .clk(clk));  // open: en, clr
  Register #(.width(5)) ID_EX_8 (.D(rd), .Q(ID_EX_8_q), .clk(clk));  // open: en, clr
  Register #(.width(32)) MEM_WB_2 (.D(ALUresul), .Q(MEM_WB_2_q), .clk(clk));  // open: en, clr
  Register #(.width(1)) ID_EX_9 (.D(J), .Q(ID_EX_9_q), .clk(clk));  // open: en, clr
  Multiplexer #(.width(5), .enable("false")) multiplexer_2 (
    .in0(ID_EX_7_q), .in1(ID_EX_8_q), .out(multiplexer_2_out), .sel(K1));
  Register #(.width(5)) EX_MEM_5 (.D(multiplexer_2_out), .Q(EX_MEM_5_q), .clk(clk));  // open: en, clr
  Multiplexer #(.width(32), .enable("false")) multiplexer_3 (
    .in0(Rdata), .in1(MEM_WB_2_q), .out(multiplexer_3_out), .sel(WD));
  Register #(.width(1)) ID_EX_10 (.D(or_1_out), .Q(ID_EX_10_q), .clk(clk));  // open: en, clr
  or or_1 (or_1_out, ALUr, ADDI);
  Register #(.width(1)) EX_MEM_6 (.D(ID_EX_9_q), .Q(K4), .clk(clk));  // open: en, clr
  Register #(.width(5)) MEM_WB_3 (.D(EX_MEM_5_q), .Q(WriteReg), .clk(clk));  // open: en, clr
  Register #(.width(1)) MEM_WB_4 (.D(EX_MEM_7_q), .Q(WD), .clk(clk));  // open: en, clr
  Register #(.width(1)) EX_MEM_7 (.D(ID_EX_10_q), .Q(EX_MEM_7_q), .clk(clk));  // open: en, clr
  not not_1 (not_1_out, clk);
  Register_file register_file_1 (
    .Read_Register_1(rs), .Read_Register_2(rt), .Write_Register(WriteReg), .Write_Data(multiplexer_3_out),
    .Read_Data_1(register_file_1_read_data_1), .Read_Data_2(register_file_1_read_data_2), .clk(not_1_out),
    .Write(WR));  // open: reset
  Register #(.width(32)) ID_EX_11 (.D(register_file_1_read_data_1), .Q(A), .clk(clk));  // open: en, clr
  Register #(.width(32)) ID_EX_12 (.D(register_file_1_read_data_2), .Q(R_rt), .clk(clk));  // open: en, clr
  Register #(.width(32)) IF_ID_2 (.D(PC_4), .Q(IF_ID_2_q), .clk(clk));  // open: en, clr
  Multiplexer #(.select(2), .width(3), .enable("false")) multiplexer_4 (
    .in0(3'b000), .in1(3'b111), .in2(3'b001), .out(OpALU), .sel({K2, K1}));  // open: in3
  Register #(.width(32)) ID_EX_13 (.D(IF_ID_2_q), .Q({ID_EX_13_q_2, ID_EX_13_q}), .clk(clk));  // open: en, clr
  Register #(.width(26)) ID_EX_14 (.D(Jin), .Q(ID_EX_14_q), .clk(clk));  // open: en, clr
  Register #(.width(32)) ID_EX_15 (.D(bit_extender_1_out), .Q(ExSig_desp), .clk(clk));  // open: en, clr
  assign bit_extender_1_out = {{16{desp[15]}}, desp};  // Bit_Extender bit_extender_1
  Shifter #(.width(32)) shifter_1 (.in(ExSig_desp), .\dist (5'b00010), .out(ExSig_dir___2));
  Adder #(.width(32)) adder_2 (
    .a(ExSig_dir___2), .b({ID_EX_13_q_2, ID_EX_13_q}), .out(adder_2_out));  // open: cin, cout
  Register #(.width(32)) EX_MEM_8 (.D({ID_EX_13_q_2, ID_EX_14_q, 2'b00}), .Q(Jump), .clk(clk));  // open: en, clr
  Register #(.width(6)) ID_EX_16 (.D(funcion), .Q(ID_EX_16_q), .clk(clk));  // open: en, clr
  Register #(.width(32)) EX_MEM_9 (.D(adder_2_out), .Q(BEQsalto), .clk(clk));  // open: en, clr
  or or_2 (or_2_out, ALUr, BEQ);
  Control_ALU control_alu_1 (.OpALU(OpALU), .funcion(ID_EX_16_q), .OUT(control_alu_1_out));
  ALU alu_1 (.A(A), .B(B), .Z(alu_1_z), .Result(alu_1_result), .Operation(control_alu_1_out));
  Multiplexer #(.width(32), .enable("false")) multiplexer_5 (.in0(ExSig_desp), .in1(R_rt), .out(B), .sel(ID_EX_17_q));
  Register #(.width(1)) ID_EX_17 (.D(or_2_out), .Q(ID_EX_17_q), .clk(clk));  // open: en, clr
  Register #(.width(1)) EX_MEM_10 (.D(alu_1_z), .Q(Z), .clk(clk));  // open: en, clr
  Register #(.width(32)) EX_MEM_11 (.D(alu_1_result), .Q(ALUresul), .clk(clk));  // open: en, clr
  Register #(.width(32)) EX_MEM_12 (.D(R_rt), .Q(EX_MEM_12_q), .clk(clk));  // open: en, clr
  Register #(.width(1)) ID_EX_18 (.D(HALT_t), .Q(ID_EX_18_q), .clk(clk));  // open: en, clr
  Data_Memory_32 data_memory_32_1 (
    .Address(ALUresul), .Write_Data(EX_MEM_12_q), .Read_Data(data_memory_32_1_read_data), .Write(WM),
    .clk(clk), .Read(RM));  // open: reset
  Register #(.width(1)) EX_MEM_13 (.D(ID_EX_18_q), .Q(EX_MEM_13_q), .clk(clk));  // open: en, clr
  Register #(.width(1)) MEM_WB_5 (.D(EX_MEM_13_q), .Q(halt), .clk(clk));  // open: en, clr
  Register #(.width(32)) MEM_WB_6 (.D(data_memory_32_1_read_data), .Q(Rdata), .clk(clk));  // open: en, clr

  // Other names for the same wires on the sheet: R_rs[31:0] = A
endmodule

module Register_file (
  input  clk,
  input  reset,
  input  [4:0] Read_Register_1,
  input  [4:0] Read_Register_2,
  input  [4:0] Write_Register,
  input  [31:0] Write_Data,
  input  Write,
  output [31:0] Read_Data_1,
  output [31:0] Read_Data_2
);

  wire decoder_1_out1, decoder_1_out2, decoder_1_out3, decoder_1_out4, decoder_1_out5, decoder_1_out6,
       decoder_1_out7, decoder_1_out8, decoder_1_out9, decoder_1_out10, decoder_1_out11, decoder_1_out12,
       decoder_1_out13, decoder_1_out14, decoder_1_out15, decoder_1_out16, decoder_1_out17, decoder_1_out18,
       decoder_1_out19, decoder_1_out20, decoder_1_out21, decoder_1_out22, decoder_1_out23, decoder_1_out24,
       decoder_1_out25, decoder_1_out26, decoder_1_out27, decoder_1_out28, decoder_1_out29, decoder_1_out30,
       decoder_1_out31;
  wire [31:0] delayer1x32_1_out, multiplexer_1_out, multiplexer_2_out, R1_q, R2_q, R3_q, R4_q, R5_q, R6_q,
       R7_q, R8_q, R9_q, R10_q, R11_q, R12_q, R13_q, R14_q, R15_q, R16_q, R17_q, R18_q, R19_q, R20_q, R21_q,
       R22_q, R23_q, R24_q, R25_q, R26_q, R27_q, R28_q, R29_q, R30_q, R31_q;

  Decoder #(.select(5), .disabled(0)) decoder_1 (
    .out1(decoder_1_out1), .out2(decoder_1_out2), .out3(decoder_1_out3), .out4(decoder_1_out4),
    .out5(decoder_1_out5), .out6(decoder_1_out6), .out7(decoder_1_out7), .out8(decoder_1_out8),
    .out9(decoder_1_out9), .out10(decoder_1_out10), .out11(decoder_1_out11), .out12(decoder_1_out12),
    .out13(decoder_1_out13), .out14(decoder_1_out14), .out15(decoder_1_out15), .out16(decoder_1_out16),
    .out17(decoder_1_out17), .out18(decoder_1_out18), .out19(decoder_1_out19), .out20(decoder_1_out20),
    .out21(decoder_1_out21), .out22(decoder_1_out22), .out23(decoder_1_out23), .out24(decoder_1_out24),
    .out25(decoder_1_out25), .out26(decoder_1_out26), .out27(decoder_1_out27), .out28(decoder_1_out28),
    .out29(decoder_1_out29), .out30(decoder_1_out30), .out31(decoder_1_out31), .sel(Write_Register),
    .en(Write));  // open: out0
  Delayer1x32 delayer1x32_1 (.in(Write_Data), .out(delayer1x32_1_out));
  Register #(.width(32)) R1 (.D(delayer1x32_1_out), .en(decoder_1_out1), .Q(R1_q), .clk(clk), .clr(reset));
  Register #(.width(32)) R2 (.D(delayer1x32_1_out), .en(decoder_1_out2), .Q(R2_q), .clk(clk), .clr(reset));
  Register #(.width(32)) R3 (.D(delayer1x32_1_out), .en(decoder_1_out3), .Q(R3_q), .clk(clk), .clr(reset));
  Register #(.width(32)) R4 (.D(delayer1x32_1_out), .en(decoder_1_out4), .Q(R4_q), .clk(clk), .clr(reset));
  Register #(.width(32)) R5 (.D(delayer1x32_1_out), .en(decoder_1_out5), .Q(R5_q), .clk(clk), .clr(reset));
  Register #(.width(32)) R6 (.D(delayer1x32_1_out), .en(decoder_1_out6), .Q(R6_q), .clk(clk), .clr(reset));
  Register #(.width(32)) R7 (.D(delayer1x32_1_out), .en(decoder_1_out7), .Q(R7_q), .clk(clk), .clr(reset));
  Register #(.width(32)) R8 (.D(delayer1x32_1_out), .en(decoder_1_out8), .Q(R8_q), .clk(clk), .clr(reset));
  Register #(.width(32)) R9 (.D(delayer1x32_1_out), .en(decoder_1_out9), .Q(R9_q), .clk(clk), .clr(reset));
  Register #(.width(32)) R10 (.D(delayer1x32_1_out), .en(decoder_1_out10), .Q(R10_q), .clk(clk), .clr(reset));
  Register #(.width(32)) R11 (.D(delayer1x32_1_out), .en(decoder_1_out11), .Q(R11_q), .clk(clk), .clr(reset));
  Register #(.width(32)) R12 (.D(delayer1x32_1_out), .en(decoder_1_out12), .Q(R12_q), .clk(clk), .clr(reset));
  Register #(.width(32)) R13 (.D(delayer1x32_1_out), .en(decoder_1_out13), .Q(R13_q), .clk(clk), .clr(reset));
  Register #(.width(32)) R14 (.D(delayer1x32_1_out), .en(decoder_1_out14), .Q(R14_q), .clk(clk), .clr(reset));
  Register #(.width(32)) R15 (.D(delayer1x32_1_out), .en(decoder_1_out15), .Q(R15_q), .clk(clk), .clr(reset));
  Register #(.width(32)) R16 (.D(delayer1x32_1_out), .en(decoder_1_out16), .Q(R16_q), .clk(clk), .clr(reset));
  Register #(.width(32)) R17 (.D(delayer1x32_1_out), .en(decoder_1_out17), .Q(R17_q), .clk(clk), .clr(reset));
  Register #(.width(32)) R18 (.D(delayer1x32_1_out), .en(decoder_1_out18), .Q(R18_q), .clk(clk), .clr(reset));
  Register #(.width(32)) R19 (.D(delayer1x32_1_out), .en(decoder_1_out19), .Q(R19_q), .clk(clk), .clr(reset));
  Register #(.width(32)) R20 (.D(delayer1x32_1_out), .en(decoder_1_out20), .Q(R20_q), .clk(clk), .clr(reset));
  Register #(.width(32)) R21 (.D(delayer1x32_1_out), .en(decoder_1_out21), .Q(R21_q), .clk(clk), .clr(reset));
  Register #(.width(32)) R22 (.D(delayer1x32_1_out), .en(decoder_1_out22), .Q(R22_q), .clk(clk), .clr(reset));
  Register #(.width(32)) R23 (.D(delayer1x32_1_out), .en(decoder_1_out23), .Q(R23_q), .clk(clk), .clr(reset));
  Register #(.width(32)) R24 (.D(delayer1x32_1_out), .en(decoder_1_out24), .Q(R24_q), .clk(clk), .clr(reset));
  Register #(.width(32)) R25 (.D(delayer1x32_1_out), .en(decoder_1_out25), .Q(R25_q), .clk(clk), .clr(reset));
  Register #(.width(32)) R26 (.D(delayer1x32_1_out), .en(decoder_1_out26), .Q(R26_q), .clk(clk), .clr(reset));
  Register #(.width(32)) R27 (.D(delayer1x32_1_out), .en(decoder_1_out27), .Q(R27_q), .clk(clk), .clr(reset));
  Register #(.width(32)) R28 (.D(delayer1x32_1_out), .en(decoder_1_out28), .Q(R28_q), .clk(clk), .clr(reset));
  Register #(.width(32)) R29 (.D(delayer1x32_1_out), .en(decoder_1_out29), .Q(R29_q), .clk(clk), .clr(reset));
  Register #(.width(32)) R30 (.D(delayer1x32_1_out), .en(decoder_1_out30), .Q(R30_q), .clk(clk), .clr(reset));
  Register #(.width(32)) R31 (.D(delayer1x32_1_out), .en(decoder_1_out31), .Q(R31_q), .clk(clk), .clr(reset));
  Multiplexer #(.select(5), .width(32), .enable("false")) multiplexer_1 (
    .in0({32{1'b0}}), .in1(R1_q), .in2(R2_q), .in3(R3_q), .in4(R4_q), .in5(R5_q), .in6(R6_q), .in7(R7_q),
    .in8(R8_q), .in9(R9_q), .in10(R10_q), .in11(R11_q), .in12(R12_q), .in13(R13_q), .in14(R14_q),
    .in15(R15_q), .in16(R16_q), .in17(R17_q), .in18(R18_q), .in19(R19_q), .in20(R20_q), .in21(R21_q),
    .in22(R22_q), .in23(R23_q), .in24(R24_q), .in25(R25_q), .in26(R26_q), .in27(R27_q), .in28(R28_q),
    .in29(R29_q), .in30(R30_q), .in31(R31_q), .out(multiplexer_1_out), .sel(Read_Register_1));
  Multiplexer #(.select(5), .width(32), .enable("false")) multiplexer_2 (
    .in0({32{1'b0}}), .in1(R1_q), .in2(R2_q), .in3(R3_q), .in4(R4_q), .in5(R5_q), .in6(R6_q), .in7(R7_q),
    .in8(R8_q), .in9(R9_q), .in10(R10_q), .in11(R11_q), .in12(R12_q), .in13(R13_q), .in14(R14_q),
    .in15(R15_q), .in16(R16_q), .in17(R17_q), .in18(R18_q), .in19(R19_q), .in20(R20_q), .in21(R21_q),
    .in22(R22_q), .in23(R23_q), .in24(R24_q), .in25(R25_q), .in26(R26_q), .in27(R27_q), .in28(R28_q),
    .in29(R29_q), .in30(R30_q), .in31(R31_q), .out(multiplexer_2_out), .sel(Read_Register_2));
  Delayer1x32 delayer1x32_2 (.in(multiplexer_1_out), .out(Read_Data_1));
  Delayer1x32 delayer1x32_3 (.in(multiplexer_2_out), .out(Read_Data_2));
endmodule

module ALU (
  input  [3:0] Operation,
  input  [31:0] A,
  input  [31:0] B,
  output Z,
  output [31:0] Result
);

  wire nor_1_out;
  wire [0:0] comparator_1_lt;
  wire [31:0] adder_1_out, and_1_out, multiplexer_1_out, multiplexer_2_out, multiplexer_3_out, not_1_out,
       not_2_out, or_1_out;

  assign not_1_out = ~A;  // NOT_Gate not_1, 32 bits wide
  assign not_2_out = ~B;  // NOT_Gate not_2, 32 bits wide
  Comparator #(.width(32)) comparator_1 (.a(A), .b(B), .lt(comparator_1_lt[0]));  // open: gt, eq
  Multiplexer #(.width(32), .enable("false")) multiplexer_1 (
    .in0(A), .in1(not_1_out), .out(multiplexer_1_out), .sel(Operation[3]));
  Multiplexer #(.width(32), .enable("false")) multiplexer_2 (
    .in0(B), .in1(not_2_out), .out(multiplexer_2_out), .sel(Operation[2]));
  assign and_1_out = multiplexer_1_out & multiplexer_2_out;  // AND_Gate and_1, 32 bits wide
  assign or_1_out = multiplexer_1_out | multiplexer_2_out;  // OR_Gate or_1, 32 bits wide
  Adder #(.width(32)) adder_1 (
    .a(multiplexer_1_out), .b(multiplexer_2_out), .out(adder_1_out), .cin(Operation[2]));  // open: cout
  Multiplexer #(.select(2), .width(32), .enable("false")) multiplexer_3 (
    .in0(and_1_out), .in1(or_1_out), .in2(adder_1_out), .in3({{31{1'b0}}, comparator_1_lt[0]}),
    .out(multiplexer_3_out), .sel(Operation[1:0]));
  nor nor_1 (nor_1_out, multiplexer_3_out[0], multiplexer_3_out[1], multiplexer_3_out[2], multiplexer_3_out[3], multiplexer_3_out[4], multiplexer_3_out[5], multiplexer_3_out[6], multiplexer_3_out[7], multiplexer_3_out[8], multiplexer_3_out[9], multiplexer_3_out[10], multiplexer_3_out[11], multiplexer_3_out[12], multiplexer_3_out[13], multiplexer_3_out[14], multiplexer_3_out[15], multiplexer_3_out[16], multiplexer_3_out[17], multiplexer_3_out[18], multiplexer_3_out[19], multiplexer_3_out[20], multiplexer_3_out[21], multiplexer_3_out[22], multiplexer_3_out[23], multiplexer_3_out[24], multiplexer_3_out[25], multiplexer_3_out[26], multiplexer_3_out[27], multiplexer_3_out[28], multiplexer_3_out[29], multiplexer_3_out[30], multiplexer_3_out[31]);
  Delayer2x32 delayer2x32_1 (.in(multiplexer_3_out), .out(Result));
  Delayer2x1 delayer2x1_1 (.in(nor_1_out), .out(Z));

  // Notes on the sheet:
  //   0001    OR
  //   Operation    Function
  //   0000    AND
  //   0010    add
  //   0110    subtract
  //   0111    set on less than
  //   1100    NOR
endmodule

module Data_Memory_32 (
  input  Write,
  input  [31:0] Address,
  input  [31:0] Write_Data,
  input  clk,
  input  reset,
  input  Read,
  output [31:0] Read_Data
);

  wire [9:0] bitselector_1_out;
  wire [31:0] delayer2x32_1_out, ram_1_data;

  BitSelector #(.width(32), .group(10)) bitselector_1 (.in(Address), .out(bitselector_1_out), .sel(2'b00));
  Delayer2x32 delayer2x32_1 (.in(Write_Data), .out(delayer2x32_1_out));
  RAM #(.dataWidth(32), .bus("separate"), .Datafile_on_reset("TG00ram.txt")) ram_1 (
    .addr(bitselector_1_out[9:2]), .din(delayer2x32_1_out), .data(ram_1_data), .str(Write), .sel(1'b1),
    .clk(clk), .ld(Read), .clr(reset));
  Delayer2x32 delayer2x32_2 (.in(ram_1_data), .out(Read_Data));

  // Notes on the sheet:
  //   Memoria de 32 bits direccionable a nivel de byte
  //   Tan solo implementadas las 256 primeras posiciones de 32 bits o 1024 bytes
endmodule

module Instruction_memory (
  input  [31:0] Read_address,
  output [31:0] Instruction
);

  wire [6:0] bitselector_1_out;
  wire [31:0] ram_1_data;

  BitSelector #(.width(30), .group(7)) bitselector_1 (.in(Read_address[31:2]), .out(bitselector_1_out), .sel(3'b000));
  RAM #(.addrWidth(7), .dataWidth(32), .bus("asynch"), .Datafile_on_reset("TG00rom.txt")) ram_1 (
    .addr(bitselector_1_out), .data(ram_1_data), .sel(1'b1), .ld(1'b1), .clr(1'b0));
  Delayer2x32 delayer2x32_1 (.in(ram_1_data), .out(Instruction));
endmodule

module InstDecoder (
  input  [31:0] IB,
  output [5:0] IB31_26,
  output [4:0] IB25_21,
  output [4:0] IB20_16,
  output [4:0] IB15_11,
  output [5:0] IB5_0,
  output [15:0] IB15_0,
  output [25:0] IB25_0
);


  assign IB5_0 = IB[5:0];
  assign IB15_0 = IB[15:0];
  assign IB15_11 = IB[15:11];
  assign IB20_16 = IB[20:16];
  assign IB25_0 = IB[25:0];
  assign IB25_21 = IB[25:21];
  assign IB31_26 = IB[31:26];
endmodule

module Control_ALU (
  input  [2:0] OpALU,
  input  [5:0] funcion,
  output [3:0] OUT
);

  wire [3:0] multiplexer_1_out;

  Multiplexer #(.select(4), .width(4), .enable("false")) multiplexer_1 (
    .in0(4'b0010), .in2(4'b0110), .in4(4'b0000), .in5(4'b0001), .in10(4'b0111), .out(multiplexer_1_out),
    .sel(funcion[3:0]));  // open: in1, in3, in6, in7, in8, in9, in11, in12, in13, in14, in15
  Multiplexer #(.select(3), .width(4), .enable("false")) multiplexer_2 (
    .in0(4'b0010), .in1(4'b0110), .in2(4'b0000), .in3(4'b0001), .in4(4'b0111), .in5(4'b1100),
    .in7(multiplexer_1_out), .out(OUT), .sel(OpALU));  // open: in6

  // Notes on the sheet:
  //   OpALU    OUT
  //    000    add
  //    001    sub
  //    010    and
  //    011    or
  //   100    set on less than
  //   101    nor
  //   111    funcion (in)
endmodule

module UNIDAD_DE_CONTROL (
  input  [5:0] OPCODE,
  output BEQ,
  output RM,
  output ADDI,
  output ALU,
  output WR,
  output WM,
  output J,
  output HALT
);

  wire LW;

  or or_1 (RM, LW, WM);
  or or_2 (WR, LW, ADDI, ALU);
  and u_BEQ (BEQ, ~OPCODE[0], ~OPCODE[1], OPCODE[2], ~OPCODE[3], ~OPCODE[4], ~OPCODE[5]);  // AND_Gate
  and u_ADDI (ADDI, ~OPCODE[0], ~OPCODE[1], ~OPCODE[2], OPCODE[3], ~OPCODE[4], ~OPCODE[5]);  // AND_Gate
  and u_ALU (ALU, ~OPCODE[0], ~OPCODE[1], ~OPCODE[2], ~OPCODE[3], ~OPCODE[4], ~OPCODE[5]);  // AND_Gate
  and SW (WM, OPCODE[0], OPCODE[1], ~OPCODE[2], OPCODE[3], ~OPCODE[4], OPCODE[5]);  // AND_Gate
  and u_LW (LW, OPCODE[0], OPCODE[1], ~OPCODE[2], ~OPCODE[3], ~OPCODE[4], OPCODE[5]);  // AND_Gate
  and u_J (J, ~OPCODE[0], OPCODE[1], ~OPCODE[2], ~OPCODE[3], ~OPCODE[4], ~OPCODE[5]);  // AND_Gate
  and u_HALT (HALT, OPCODE[0], OPCODE[1], OPCODE[2], OPCODE[3], OPCODE[4], OPCODE[5]);

  // Other names for the same wires on the sheet: SW = WM
endmodule
